// Logisim project cpu.circ as structural Verilog: 6 circuits, main circuit main
module main (
);

  wire Br, MemRead, MemWrite, ReadDataM, RegWrite, WriteDataM;
  wire [2:0] ALUop;
  wire [4:0] ReadReg1, ReadReg2, ReadReg3, WriteReg;
  wire [23:0] Bdst;
  wire [31:0] ALUout, Instr, RegData1, Regdata1_t, RegData2, Regdata2_t, RegData3, Regdata3_t, RegDataW;

  PC pc_1 (.Bdst(Bdst), .Br(Br), .Instr(Instr));
  ControlUnit controlunit_1 (.Instr(Instr));  // open: WriteDataM, ReadDataM, MemRead, MemWrite, ReadReg3, ReadReg2, ReadReg1, WriteReg, Br, RegWrite, ALUop
  // RegFile regfile_1: pin names not known; wires that end beside it: RegDataW, ReadReg1, ReadReg2, ReadReg3, RegWrite, WriteReg, RegData1, RegData2, RegData3
  ALU alu_1 (
    .RegData1(Regdata1_t), .RegData2(Regdata2_t), .RegData3(Regdata3_t), .ALUop(ALUop), .ALUout(ALUout),
    .Bdst(Bdst));
  MEM mem_1 (
    .MemRead(MemRead), .MemWrite(MemWrite), .WriteDataM(WriteDataM), .ReadDataM(ReadDataM), .ALUout(ALUout),
    .RegDataW(RegDataW));

  // Notes on the sheet:
  //   Stage 1: IF
  //   Stage 2: ID
  //   Stage 3: EX
endmodule

module PC (
  input  [23:0] Bdst,
  input  Br,
  output [31:0] Instr
);

  wire CLK;
  wire [23:0] adder_1_out, nextPC, PC;

  Clock clock_1 (.out(CLK));
  Register #(.width(24)) register_1 (.D(nextPC), .en(1'b1), .clk(CLK), .Q(PC));  // open: clr
  Adder #(.width(24)) adder_1 (.a(PC), .b(24'h1), .out(adder_1_out));  // open: cin, cout
  RAM #(.addrWidth(24), .dataWidth(32), .enables("line")) Instruction_Memory (
    .addr(PC), .clk(CLK), .dout(Instr));  // open: we, din
  Multiplexer #(.width(24)) multiplexer_1 (.in0(adder_1_out), .in1(Bdst), .out(nextPC), .sel(Br));
endmodule

module RegFile (
  input  [31:0] RegDataW,
  input  RegWrite,
  input  [4:0] WriteReg,
  input  [4:0] ReadReg1,
  input  [4:0] ReadReg2,
  input  [4:0] ReadReg3,
  output [31:0] RegData1,
  output [31:0] RegData2,
  output [31:0] RegData3
);

  wire CLK, WE0, WE1, WE2, WE3, WE4, WE5, WE6, WE7, WE8, WE9, WE10, WE11, WE12, WE13, WE14, WE15, WE16, WE17,
       WE18, WE19, WE20, WE21, WE22, WE23, WE24, WE25, WE26, WE27, WE28, WE29, WE30, WE31, WR0, WR1, WR2,
       WR3, WR4, WR5, WR6, WR7, WR8, WR9, WR10, WR11, WR12, WR13, WR14, WR15, WR16, WR17, WR18, WR19, WR20,
       WR21, WR22, WR23, WR24, WR25, WR26, WR27, WR28, WR29, WR30, WR31;
  wire [31:0] R0d, R1d, R2d, R3d, R4d, R5d, R6d, R7d, R8d, R9d, R10d, R11d, R12d, R13d, R14d, R15d, R16d,
       R17d, R18d, R19d, R20d, R21d, R22d, R23d, R24d, R25d, R26d, R27d, R28d, R29d, R30d, R31d;

  Decoder #(.select(5)) decoder_1 (
    .out0(WR0), .out1(WR1), .out2(WR2), .out3(WR3), .out4(WR4), .out5(WR5), .out6(WR6), .out7(WR7),
    .out8(WR8), .out9(WR9), .out10(WR10), .out11(WR11), .out12(WR12), .out13(WR13), .out14(WR14),
    .out15(WR15), .out16(WR16), .out17(WR17), .out18(WR18), .out19(WR19), .out20(WR20), .out21(WR21),
    .out22(WR22), .out23(WR23), .out24(WR24), .out25(WR25), .out26(WR26), .out27(WR27), .out28(WR28),
    .out29(WR29), .out30(WR30), .out31(WR31), .sel(WriteReg));  // open: en
  Clock clock_1 (.out(CLK));
  and and_1 (WE0, RegWrite, WR0);
  and and_2 (WE1, RegWrite, WR1);
  and and_3 (WE2, RegWrite, WR2);
  and and_4 (WE3, RegWrite, WR3);
  and and_5 (WE4, RegWrite, WR4);
  and and_6 (WE5, RegWrite, WR5);
  and and_7 (WE6, RegWrite, WR6);
  and and_8 (WE7, RegWrite, WR7);
  and and_9 (WE8, RegWrite, WR8);
  and and_10 (WE9, RegWrite, WR9);
  and and_11 (WE10, RegWrite, WR10);
  and and_12 (WE11, RegWrite, WR11);
  and and_13 (WE12, RegWrite, WR12);
  and and_14 (WE13, RegWrite, WR13);
  and and_15 (WE14, RegWrite, WR14);
  and and_16 (WE15, RegWrite, WR15);
  and and_17 (WE16, RegWrite, WR16);
  and and_18 (WE17, RegWrite, WR17);
  and and_19 (WE18, RegWrite, WR18);
  and and_20 (WE19, RegWrite, WR19);
  and and_21 (WE20, RegWrite, WR20);
  and and_22 (WE21, RegWrite, WR21);
  and and_23 (WE22, RegWrite, WR22);
  and and_24 (WE23, RegWrite, WR23);
  and and_25 (WE24, RegWrite, WR24);
  and and_26 (WE25, RegWrite, WR25);
  and and_27 (WE26, RegWrite, WR26);
  and and_28 (WR27, RegWrite, WR27);
  and and_29 (WR28, RegWrite, WR28);
  and and_30 (WR29, RegWrite, WR29);
  and and_31 (WE30, RegWrite, WR30);
  and and_32 (WE31, RegWrite, WR31);
  Register #(.width(32)) R0 (.D(RegDataW), .en(WE0), .clk(CLK), .Q(R0d));  // open: clr
  Register #(.width(32)) R1 (.D(RegDataW), .en(WE1), .clk(CLK), .Q(R1d));  // open: clr
  Register #(.width(32)) R2 (.D(RegDataW), .en(WE2), .clk(CLK), .Q(R2d));  // open: clr
  Register #(.width(32)) R3 (.D(RegDataW), .en(WE3), .clk(CLK), .Q(R3d));  // open: clr
  Register #(.width(32)) R4 (.D(RegDataW), .en(WE4), .clk(CLK), .Q(R4d));  // open: clr
  Register #(.width(32)) R5 (.D(RegDataW), .en(WE5), .clk(CLK), .Q(R5d));  // open: clr
  Register #(.width(32)) R6 (.D(RegDataW), .en(WE6), .clk(CLK), .Q(R6d));  // open: clr
  Register #(.width(32)) R7 (.D(RegDataW), .en(WE7), .clk(CLK), .Q(R7d));  // open: clr
  Multiplexer #(.select(5), .width(32)) multiplexer_1 (
    .in0(R0d), .in1(R1d), .in2(R2d), .in3(R3d), .in4(R4d), .in5(R5d), .in6(R6d), .in7(R7d), .in8(R8d),
    .in9(R9d), .in10(R10d), .in11(R11d), .in12(R12d), .in13(R13d), .in14(R14d), .in15(R15d), .in16(R16d),
    .in17(R17d), .in18(R18d), .in19(R19d), .in20(R20d), .in21(R21d), .in22(R22d), .in23(R23d), .in24(R24d),
    .in25(R25d), .in26(R26d), .in27(R27d), .in28(R28d), .in29(R29d), .in30(R30d), .in31(R31d),
    .out(RegData1), .sel(ReadReg1));
  Register #(.width(32)) R8 (.D(RegDataW), .en(WE8), .clk(CLK), .Q(R8d));  // open: clr
  Register #(.width(32)) R9 (.D(RegDataW), .en(WE9), .clk(CLK), .Q(R9d));  // open: clr
  Register #(.width(32)) R10 (.D(RegDataW), .en(WE10), .clk(CLK), .Q(R10d));  // open: clr
  Register #(.width(32)) R11 (.D(RegDataW), .en(WE11), .clk(CLK), .Q(R11d));  // open: clr
  Register #(.width(32)) R12 (.D(RegDataW), .en(WE12), .clk(CLK), .Q(R12d));  // open: clr
  Register #(.width(32)) R13 (.D(RegDataW), .en(WE13), .clk(CLK), .Q(R13d));  // open: clr
  Register #(.width(32)) R14 (.D(RegDataW), .en(WE14), .clk(CLK), .Q(R14d));  // open: clr
  Register #(.width(32)) R15 (.D(RegDataW), .en(WE15), .clk(CLK), .Q(R15d));  // open: clr
  Multiplexer #(.select(5), .width(32)) multiplexer_2 (
    .in0(R0d), .in1(R1d), .in2(R2d), .in3(R3d), .in4(R4d), .in5(R5d), .in6(R6d), .in7(R7d), .in8(R8d),
    .in9(R9d), .in10(R10d), .in11(R11d), .in12(R12d), .in13(R13d), .in14(R14d), .in15(R15d), .in16(R16d),
    .in17(R17d), .in18(R18d), .in19(R19d), .in20(R20d), .in21(R21d), .in22(R22d), .in23(R23d), .in24(R24d),
    .in25(R25d), .in26(R26d), .in27(R27d), .in28(R28d), .in29(R29d), .in30(R30d), .in31(R31d),
    .out(RegData3), .sel(ReadReg3));
  Register #(.width(32)) R16 (.D(RegDataW), .en(WE16), .clk(CLK), .Q(R16d));  // open: clr
  Register #(.width(32)) R17 (.D(RegDataW), .en(WE17), .clk(CLK), .Q(R17d));  // open: clr
  Register #(.width(32)) R18 (.D(RegDataW), .en(WE18), .clk(CLK), .Q(R18d));  // open: clr
  Register #(.width(32)) R19 (.D(RegDataW), .en(WE19), .clk(CLK), .Q(R19d));  // open: clr
  Register #(.width(32)) R20 (.D(RegDataW), .en(WE20), .clk(CLK), .Q(R20d));  // open: clr
  Register #(.width(32)) R21 (.D(RegDataW), .en(WE21), .clk(CLK), .Q(R21d));  // open: clr
  Register #(.width(32)) R22 (.D(RegDataW), .en(WE22), .clk(CLK), .Q(R22d));  // open: clr
  Register #(.width(32)) R23 (.D(RegDataW), .en(WE23), .clk(CLK), .Q(R23d));  // open: clr
  Multiplexer #(.select(5), .width(32)) multiplexer_3 (
    .in0(R0d), .in1(R1d), .in2(R2d), .in3(R3d), .in4(R4d), .in5(R5d), .in6(R6d), .in7(R7d), .in8(R8d),
    .in9(R9d), .in10(R10d), .in11(R11d), .in12(R12d), .in13(R13d), .in14(R14d), .in15(R15d), .in16(R16d),
    .in17(R17d), .in18(R18d), .in19(R19d), .in20(R20d), .in21(R21d), .in22(R22d), .in23(R23d), .in24(R24d),
    .in25(R25d), .in26(R26d), .in27(R27d), .in28(R28d), .in29(R29d), .in30(R30d), .in31(R31d),
    .out(RegData2), .sel(ReadReg2));
  Register #(.width(32)) R24 (.D(RegDataW), .en(WE24), .clk(CLK), .Q(R24d));  // open: clr
  Register #(.width(32)) R25 (.D(RegDataW), .en(WE25), .clk(CLK), .Q(R25d));  // open: clr
  Register #(.width(32)) R26 (.D(RegDataW), .en(WE26), .clk(CLK), .Q(R26d));  // open: clr
  Register #(.width(32)) R27 (.D(RegDataW), .en(WE27), .clk(CLK), .Q(R27d));  // open: clr
  Register #(.width(32)) R28 (.D(RegDataW), .en(WE28), .clk(CLK), .Q(R28d));  // open: clr
  Register #(.width(32)) R29 (.D(RegDataW), .en(WE29), .clk(CLK), .Q(R29d));  // open: clr
  Register #(.width(32)) R30_CMP (.D(RegDataW), .en(WE30), .clk(CLK), .Q(R30d));  // open: clr
  Register #(.width(32)) R31_LR (.D(RegDataW), .en(WE31), .clk(CLK), .Q(R31d));  // open: clr
endmodule

module ALU (
  input  [31:0] RegData1,
  input  [31:0] RegData2,
  input  [31:0] RegData3,
  input  [2:0] ALUop,
  output [31:0] ALUout,
  output [23:0] Bdst
);

  Adder adder_1 ();  // open: a, b, out, cin, cout
  Subtractor subtractor_1 ();  // open: a, b, out, bin, bout
  Multiplier multiplier_1 ();  // open: a, b, out, cin, cout
  Divider divider_1 ();  // open: a, b, out, upper, rem
  Negator negator_1 ();  // open: in, out
  Shifter shifter_1 ();  // open: in, dist, out
  Shifter #(.shift("lr")) shifter_2 ();  // open: in, dist, out
  Shifter #(.shift("ar")) shifter_3 ();  // open: in, dist, out
  // AND_Gate and_1 is placed but not wired
  // OR_Gate or_1 is placed but not wired
  // XOR_Gate xor_1 is placed but not wired
endmodule

module ControlUnit (
  input  [31:0] Instr,
  output WriteDataM,
  output ReadDataM,
  output MemRead,
  output MemWrite,
  output [4:0] ReadReg3,
  output [4:0] ReadReg2,
  output [4:0] ReadReg1,
  output [4:0] WriteReg,
  output Br,
  output RegWrite,
  output [4:0] ALUop
);

  wire and_4_out, and_5_out, and_6_out, comparator_1_eq, comparator_2_eq, comparator_3_eq, comparator_4_eq,
       comparator_5_eq, comparator_6_eq, comparator_7_eq, comparator_8_eq, comparator_9_eq, comparator_10_eq,
       comparator_11_eq, comparator_12_eq, comparator_13_eq, comparator_14_eq, comparator_15_eq,
       comparator_16_eq, not_1_out;

  Comparator #(.width(1)) comparator_1 (.a(Instr[30]), .b(1'b1), .eq(comparator_1_eq));  // open: gt, lt
  Comparator #(.width(1)) comparator_2 (.a(Instr[31]), .b(1'b0), .eq(comparator_2_eq));  // open: gt, lt
  Comparator #(.width(1)) comparator_3 (.a(Instr[26]), .b(1'b0), .eq(comparator_3_eq));  // open: gt, lt
  Comparator #(.width(1)) comparator_4 (.a(Instr[30]), .b(1'b1), .eq(comparator_4_eq));  // open: gt, lt
  Comparator #(.width(1)) comparator_5 (.a(Instr[31]), .b(1'b0), .eq(comparator_5_eq));  // open: gt, lt
  Comparator #(.width(1)) comparator_6 (.a(Instr[26]), .b(1'b1), .eq(comparator_6_eq));  // open: gt, lt
  Comparator #(.width(1)) comparator_7 (.a(Instr[30]), .b(1'b0), .eq(comparator_7_eq));  // open: gt, lt
  Comparator #(.width(1)) comparator_8 (.a(Instr[31]), .b(1'b1), .eq(comparator_8_eq));  // open: gt, lt
  Comparator #(.width(1)) comparator_9 (.a(Instr[31]), .b(1'b0), .eq(comparator_9_eq));  // open: gt, lt
  Comparator #(.width(1)) comparator_10 (.a(Instr[30]), .b(1'b0), .eq(comparator_10_eq));  // open: gt, lt
  Comparator #(.width(1)) comparator_11 (.a(Instr[31]), .b(1'b0), .eq(comparator_11_eq));  // open: gt, lt
  Comparator #(.width(1)) comparator_12 (.a(Instr[30]), .b(1'b1), .eq(comparator_12_eq));  // open: gt, lt
  not not_1 (not_1_out, comparator_13_eq);
  Comparator #(.width(1)) comparator_13 (.a(Instr[26]), .b(1'b1), .eq(comparator_13_eq));  // open: gt, lt
  Comparator #(.width(1)) comparator_14 (.a(Instr[31]), .b(1'b1), .eq(comparator_14_eq));  // open: gt, lt
  Comparator #(.width(1)) comparator_15 (.a(Instr[30]), .b(1'b1), .eq(comparator_15_eq));  // open: gt, lt
  Comparator #(.width(1)) comparator_16 (.a(Instr[27]), .b(1'b1), .eq(comparator_16_eq));  // open: gt, lt
  and and_1 (MemRead, comparator_1_eq, comparator_2_eq, comparator_3_eq);
  and and_2 (MemWrite, comparator_4_eq, comparator_5_eq, comparator_6_eq);
  and and_3 (Br, comparator_7_eq, comparator_8_eq);
  and and_4 (and_4_out, comparator_9_eq, comparator_10_eq);
  and and_5 (and_5_out, comparator_11_eq, not_1_out);
  and and_6 (and_6_out, comparator_14_eq, comparator_16_eq);
  or or_1 (RegWrite, and_4_out, and_5_out, and_6_out);

  assign ReadReg1 = Instr[20:16];
  assign ReadReg2 = Instr[15:11];
  assign ReadReg3 = Instr[10:6];
  assign WriteReg = Instr[25:21];

  // Notes on the sheet:
  //   Opcode
  //   B/BEQ/...?
  //   Arithmetic?
  //   LDR, ADR?
  //   MOV?
  //   LDR or STR?
  //   LDR
  //   STR
  //   Instr w/o Opcode
endmodule

module MEM (
  input  MemRead,
  input  MemWrite,
  input  WriteDataM,
  input  ReadDataM,
  input  [31:0] ALUout,
  output [31:0] RegDataW
);

  wire CLK;

  Clock clock_1 (.out(CLK));
  RAM #(.addrWidth(24), .dataWidth(32), .enables("line")) DRAM (.clk(CLK));  // open: addr, we, din, dout
endmodule
